// Logisim project ALU_template.circ as structural Verilog: 24 circuits, main circuit ALU32
module Arithmetic (
  input  [31:0] A,
  input  [31:0] B,
  input  [3:0] Op,
  output [31:0] O,
  output V
);

  wire [31:0] bit_extender_1_out, xor_1_out;

  assign xor_1_out = B ^ bit_extender_1_out;  // XOR_Gate xor_1, 32 bits wide
  assign bit_extender_1_out = {{31{Op[2]}}, Op[2]};  // Bit_Extender bit_extender_1
  Add32 add32_1 (.A(A), .B(xor_1_out), .Cin(Op[2]), .V(V), .C(O));
endmodule

module Comparators (
  input  [31:0] A,
  input  [31:0] B,
  input  [3:0] Op,
  output [31:0] O,
  output V
);

  wire eq32_1_o, gt32_1_o, le32_1_o, multiplexer_1_out, multiplexer_2_out, multiplexer_3_out, neq32_1_o;

  Gt32 gt32_1 (.A(A), .Bit(Op[3]), .O(gt32_1_o));
  Le32 le32_1 (.A(A), .Bit(Op[3]), .O(le32_1_o));
  Eq32 eq32_1 (.A(A), .B(B), .O(eq32_1_o));
  Neq32 neq32_1 (.A(A), .B(B), .O(neq32_1_o));
  Multiplexer #(.enable("false")) multiplexer_1 (.in0(neq32_1_o), .in1(eq32_1_o), .out(multiplexer_1_out), .sel(Op[0]));
  Multiplexer #(.enable("false")) multiplexer_2 (.in0(le32_1_o), .in1(gt32_1_o), .out(multiplexer_2_out), .sel(Op[0]));
  Multiplexer #(.enable("false")) multiplexer_3 (
    .in0(multiplexer_1_out), .in1(multiplexer_2_out), .out(multiplexer_3_out), .sel(Op[1]));
  assign O = {{31{1'b0}}, multiplexer_3_out};  // Bit_Extender bit_extender_1

  assign V = Op[3];
endmodule

module Gates (
  input  [31:0] A,
  input  [31:0] B,
  input  [3:0] Op,
  output [31:0] O,
  output V
);

  wire xnor_1_out;
  wire [31:0] and_1_out, multiplexer_1_out, multiplexer_2_out, nor_1_out, or_1_out, xor_1_out;

  assign or_1_out = A | B;  // OR_Gate or_1, 32 bits wide
  assign and_1_out = A & B;  // AND_Gate and_1, 32 bits wide
  assign nor_1_out = ~(A | B);  // NOR_Gate nor_1, 32 bits wide
  assign xor_1_out = A ^ B;  // XOR_Gate xor_1, 32 bits wide
  Multiplexer #(.width(32), .enable("false")) multiplexer_1 (
    .in0(xor_1_out), .in1(nor_1_out), .out(multiplexer_1_out), .sel(Op[0]));
  Multiplexer #(.width(32), .enable("false")) multiplexer_2 (
    .in0(or_1_out), .in1(and_1_out), .out(multiplexer_2_out), .sel(Op[0]));
  xnor xnor_1 (xnor_1_out, Op[1], Op[2]);
  not not_1 (V, xnor_1_out);
  Multiplexer #(.width(32), .enable("false")) multiplexer_3 (
    .in0(multiplexer_1_out), .in1(multiplexer_2_out), .out(O), .sel(Op[3]));
endmodule

module Add32 (
  input  [31:0] A,
  input  [31:0] B,
  input  Cin,
  output V,
  output [31:0] C
);

  wire eightbitadder_1_cout, fourbitadder_1_cout, onebitadder_1_cout, onebitadder_2_cout,
       sixteenbitadder_1_cout, twobitadder_1_cout;

  SixteenBitAdder sixteenbitadder_1 (.A(A[15:0]), .Cin(Cin), .B(B[15:0]), .Cout(sixteenbitadder_1_cout), .C(C[15:0]));
  EightBitAdder eightbitadder_1 (
    .A(A[23:16]), .Cin(sixteenbitadder_1_cout), .B(B[23:16]), .Cout(eightbitadder_1_cout), .C(C[23:16]));
  FourBitAdder fourbitadder_1 (
    .A(A[27:24]), .Cin(eightbitadder_1_cout), .B(B[27:24]), .Cout(fourbitadder_1_cout), .C(C[27:24]));
  TwoBitAdder twobitadder_1 (
    .A(A[29:28]), .Cin(fourbitadder_1_cout), .B(B[29:28]), .Cout(twobitadder_1_cout), .C(C[29:28]));
  OneBitAdder onebitadder_1 (.A(A[30]), .B(B[30]), .Cin(twobitadder_1_cout), .S(C[30]), .Cout(onebitadder_1_cout));
  OneBitAdder onebitadder_2 (.A(A[31]), .B(B[31]), .Cin(onebitadder_1_cout), .S(C[31]), .Cout(onebitadder_2_cout));
  xor xor_1 (V, onebitadder_1_cout, onebitadder_2_cout);
endmodule

module LeftShift32 (
  input  [4:0] Sa,
  input  [31:0] B,
  input  Cin,
  output [31:0] C
);

  wire [31:0] lshift1_1_o, lshift2_1_out_3, lshift4_1_out_3, lshift8_1_out_3, lshift16_1_out_3,
       multiplexer_1_out, multiplexer_2_out, multiplexer_3_out, multiplexer_4_out;

  Multiplexer #(.width(32), .enable("false")) multiplexer_1 (
    .in0(B), .in1(lshift1_1_o), .out(multiplexer_1_out), .sel(Sa[0]));
  Multiplexer #(.width(32), .enable("false")) multiplexer_2 (
    .in0(multiplexer_1_out), .in1(lshift2_1_out_3), .out(multiplexer_2_out), .sel(Sa[1]));
  Multiplexer #(.width(32), .enable("false")) multiplexer_3 (
    .in0(multiplexer_2_out), .in1(lshift4_1_out_3), .out(multiplexer_3_out), .sel(Sa[2]));
  Multiplexer #(.width(32), .enable("false")) multiplexer_4 (
    .in0(multiplexer_3_out), .in1(lshift8_1_out_3), .out(multiplexer_4_out), .sel(Sa[3]));
  Multiplexer #(.width(32), .enable("false")) multiplexer_5 (
    .in0(multiplexer_4_out), .in1(lshift16_1_out_3), .out(C), .sel(Sa[4]));
  LSHIFT1 lshift1_1 (.B(B), .Cin(Cin), .O(lshift1_1_o));
  LSHIFT2 lshift2_1 (.in_1(multiplexer_1_out), .in_2(Cin), .out_3(lshift2_1_out_3));
  LSHIFT4 lshift4_1 (.in_1(multiplexer_2_out), .in_2(Cin), .out_3(lshift4_1_out_3));
  LSHIFT8 lshift8_1 (.in_1(multiplexer_3_out), .in_2(Cin), .out_3(lshift8_1_out_3));
  LSHIFT16 lshift16_1 (.in_1(multiplexer_4_out), .in_2(Cin), .out_3(lshift16_1_out_3));
endmodule

module ALU32 (
  input  [31:0] A,
  input  [31:0] B,
  input  [3:0] Op,
  input  [4:0] Sa,
  output [31:0] C,
  output V
);

  wire and_1_out, arithmetic_1_v, comparators_1_v, equality3_1_o, gates_1_v, multiplexer_3_out,
       multiplexer_4_out, multiplexer_6_out, shifters_1_v, xnor_1_out;
  wire [31:0] arithmetic_1_o, comparators_1_o, gates_1_o, multiplexer_1_out, multiplexer_2_out,
       multiplexer_5_out, shifters_1_o;

  Gates gates_1 (.A(A), .B(B), .Op(Op), .O(gates_1_o), .V(gates_1_v));
  Shifters shifters_1 (.B(B), .Sa(Sa), .Op(Op), .O(shifters_1_o), .V(shifters_1_v));
  Arithmetic arithmetic_1 (.A(A), .B(B), .Op(Op), .O(arithmetic_1_o), .V(arithmetic_1_v));
  Comparators comparators_1 (.A(A), .B(B), .Op(Op), .O(comparators_1_o), .V(comparators_1_v));
  Multiplexer #(.width(32), .enable("false")) multiplexer_1 (
    .in0(comparators_1_o), .in1(shifters_1_o), .out(multiplexer_1_out), .sel(Op[3]));
  Equality3 equality3_1 (.bit2(Op[2]), .bit1(Op[3]), .bit0(Op[1]), .O(equality3_1_o));
  Multiplexer #(.width(32), .enable("false")) multiplexer_2 (
    .in0(multiplexer_1_out), .in1(gates_1_o), .out(multiplexer_2_out), .sel(xnor_1_out));
  and and_1 (and_1_out, Op[3], Op[1]);
  Multiplexer #(.enable("false")) multiplexer_3 (
    .in0(comparators_1_v), .in1(shifters_1_v), .out(multiplexer_3_out), .sel(Op[3]));
  xnor xnor_1 (xnor_1_out, Op[2], Op[1]);
  Multiplexer #(.enable("false")) multiplexer_4 (
    .in0(multiplexer_3_out), .in1(gates_1_v), .out(multiplexer_4_out), .sel(xnor_1_out));
  Multiplexer #(.width(32), .enable("false")) multiplexer_5 (
    .in0(multiplexer_2_out), .in1(shifters_1_o), .out(multiplexer_5_out), .sel(equality3_1_o));
  Multiplexer #(.enable("false")) multiplexer_6 (
    .in0(multiplexer_4_out), .in1(shifters_1_v), .out(multiplexer_6_out), .sel(equality3_1_o));
  Multiplexer #(.width(32), .enable("false")) multiplexer_7 (
    .in0(multiplexer_5_out), .in1(arithmetic_1_o), .out(C), .sel(and_1_out));
  Multiplexer #(.enable("false")) multiplexer_8 (
    .in0(multiplexer_6_out), .in1(arithmetic_1_v), .out(V), .sel(and_1_out));

  // Notes on the sheet:
  //   shift or comp
  //   gates or sth
  //   shift right or sth
  //   add or sth
endmodule

module LSHIFT1 (
  input  [31:0] B,
  input  Cin,
  output [31:0] O
);


  assign O = {B[30:0], Cin};
endmodule

module LSHIFT2 (
  input  [31:0] in_1,
  input  in_2,
  output [31:0] out_3
);

  wire [31:0] lshift1_1_o;

  LSHIFT1 lshift1_1 (.B(in_1), .Cin(in_2), .O(lshift1_1_o));
  LSHIFT1 lshift1_2 (.B(lshift1_1_o), .Cin(in_2), .O(out_3));
endmodule

module LSHIFT4 (
  input  [31:0] in_1,
  input  in_2,
  output [31:0] out_3
);

  wire [31:0] lshift2_1_out_3;

  LSHIFT2 lshift2_1 (.in_1(in_1), .in_2(in_2), .out_3(lshift2_1_out_3));
  LSHIFT2 lshift2_2 (.in_1(lshift2_1_out_3), .in_2(in_2), .out_3(out_3));
endmodule

module LSHIFT8 (
  input  [31:0] in_1,
  input  in_2,
  output [31:0] out_3
);

  wire [31:0] lshift4_1_out_3;

  LSHIFT4 lshift4_1 (.in_1(in_1), .in_2(in_2), .out_3(lshift4_1_out_3));
  LSHIFT4 lshift4_2 (.in_1(lshift4_1_out_3), .in_2(in_2), .out_3(out_3));
endmodule

module LSHIFT16 (
  input  [31:0] in_1,
  input  in_2,
  output [31:0] out_3
);

  wire [31:0] lshift8_1_out_3;

  LSHIFT8 lshift8_1 (.in_1(in_1), .in_2(in_2), .out_3(lshift8_1_out_3));
  LSHIFT8 lshift8_2 (.in_1(lshift8_1_out_3), .in_2(in_2), .out_3(out_3));
endmodule

module OneBitAdder (
  input  A,
  input  B,
  input  Cin,
  output S,
  output Cout
);

  wire and_1_out, and_2_out, xor_1_out;

  and and_1 (and_1_out, A, B);
  xor xor_1 (xor_1_out, A, B);
  and and_2 (and_2_out, Cin, xor_1_out);
  xor xor_2 (S, xor_1_out, Cin);
  or or_1 (Cout, and_2_out, and_1_out);
endmodule

module FourBitAdder (
  input  [3:0] A,
  input  Cin,
  input  [3:0] B,
  output Cout,
  output [3:0] C
);

  wire onebitadder_1_cout, onebitadder_2_cout, onebitadder_3_cout;

  OneBitAdder onebitadder_1 (.A(A[0]), .B(B[0]), .Cin(Cin), .S(C[0]), .Cout(onebitadder_1_cout));
  OneBitAdder onebitadder_2 (.A(A[1]), .B(B[1]), .Cin(onebitadder_1_cout), .S(C[1]), .Cout(onebitadder_2_cout));
  OneBitAdder onebitadder_3 (.A(A[2]), .B(B[2]), .Cin(onebitadder_2_cout), .S(C[2]), .Cout(onebitadder_3_cout));
  OneBitAdder onebitadder_4 (.A(A[3]), .B(B[3]), .Cin(onebitadder_3_cout), .S(C[3]), .Cout(Cout));
endmodule

module EightBitAdder (
  input  [7:0] A,
  input  Cin,
  input  [7:0] B,
  output Cout,
  output [7:0] C
);

  wire fourbitadder_1_cout;

  FourBitAdder fourbitadder_1 (.A(A[3:0]), .Cin(Cin), .B(B[3:0]), .Cout(fourbitadder_1_cout), .C(C[3:0]));
  FourBitAdder fourbitadder_2 (.A(A[7:4]), .Cin(fourbitadder_1_cout), .B(B[7:4]), .Cout(Cout), .C(C[7:4]));
endmodule

module SixteenBitAdder (
  input  [15:0] A,
  input  Cin,
  input  [15:0] B,
  output Cout,
  output [15:0] C
);

  wire eightbitadder_1_cout;

  EightBitAdder eightbitadder_1 (.A(A[7:0]), .Cin(Cin), .B(B[7:0]), .Cout(eightbitadder_1_cout), .C(C[7:0]));
  EightBitAdder eightbitadder_2 (.A(A[15:8]), .Cin(eightbitadder_1_cout), .B(B[15:8]), .Cout(Cout), .C(C[15:8]));
endmodule

module TwoBitAdder (
  input  [1:0] A,
  input  Cin,
  input  [1:0] B,
  output Cout,
  output [1:0] C
);

  wire onebitadder_1_cout;

  OneBitAdder onebitadder_1 (.A(A[0]), .B(B[0]), .Cin(Cin), .S(C[0]), .Cout(onebitadder_1_cout));
  OneBitAdder onebitadder_2 (.A(A[1]), .B(B[1]), .Cin(onebitadder_1_cout), .S(C[1]), .Cout(Cout));
endmodule

module Neq10 (
  input  [9:0] A,
  input  [9:0] B,
  output O
);

  wire xnor_1_out, xnor_2_out, xnor_3_out, xnor_4_out, xnor_5_out, xnor_6_out, xnor_7_out, xnor_8_out,
       xnor_9_out, xnor_10_out;

  xnor xnor_1 (xnor_1_out, A[0], B[0]);
  xnor xnor_2 (xnor_2_out, A[1], B[1]);
  xnor xnor_3 (xnor_3_out, A[2], B[2]);
  xnor xnor_4 (xnor_4_out, A[3], B[3]);
  xnor xnor_5 (xnor_5_out, A[4], B[4]);
  xnor xnor_6 (xnor_6_out, A[5], B[5]);
  xnor xnor_7 (xnor_7_out, A[6], B[6]);
  xnor xnor_8 (xnor_8_out, A[7], B[7]);
  xnor xnor_9 (xnor_9_out, A[8], B[8]);
  xnor xnor_10 (xnor_10_out, A[9], B[9]);
  and and_1 (O, xnor_1_out, xnor_2_out, xnor_3_out, xnor_4_out, xnor_5_out, xnor_6_out, xnor_7_out, xnor_8_out, xnor_9_out, xnor_10_out);
endmodule

module Neq11 (
  input  [10:0] A,
  input  [10:0] B,
  output O
);

  wire xnor_1_out, xnor_2_out, xnor_3_out, xnor_4_out, xnor_5_out, xnor_6_out, xnor_7_out, xnor_8_out,
       xnor_9_out, xnor_10_out, xnor_11_out;

  xnor xnor_1 (xnor_1_out, A[0], B[0]);
  xnor xnor_2 (xnor_2_out, A[1], B[1]);
  xnor xnor_3 (xnor_3_out, A[2], B[2]);
  xnor xnor_4 (xnor_4_out, A[3], B[3]);
  xnor xnor_5 (xnor_5_out, A[4], B[4]);
  xnor xnor_6 (xnor_6_out, A[5], B[5]);
  xnor xnor_7 (xnor_7_out, A[6], B[6]);
  xnor xnor_8 (xnor_8_out, A[7], B[7]);
  xnor xnor_9 (xnor_9_out, A[8], B[8]);
  xnor xnor_10 (xnor_10_out, A[9], B[9]);
  xnor xnor_11 (xnor_11_out, A[10], B[10]);
  and and_1 (O, xnor_1_out, xnor_2_out, xnor_3_out, xnor_4_out, xnor_5_out, xnor_6_out, xnor_7_out, xnor_8_out, xnor_9_out, xnor_10_out, xnor_11_out);
endmodule

module Neq32 (
  input  [31:0] A,
  input  [31:0] B,
  output O
);

  wire and_1_out, neq10_1_o, neq11_1_o, neq11_2_o;

  Neq11 neq11_1 (.A(A[10:0]), .B(B[10:0]), .O(neq11_1_o));
  Neq11 neq11_2 (.A(A[21:11]), .B(B[21:11]), .O(neq11_2_o));
  Neq10 neq10_1 (.A(A[31:22]), .B(B[31:22]), .O(neq10_1_o));
  and and_1 (and_1_out, neq11_1_o, neq11_2_o, neq10_1_o);
  not not_1 (O, and_1_out);
endmodule

module Eq32 (
  input  [31:0] A,
  input  [31:0] B,
  output O
);

  wire neq32_1_o;

  Neq32 neq32_1 (.A(A), .B(B), .O(neq32_1_o));
  not not_1 (O, neq32_1_o);
endmodule

module Le32 (
  input  [31:0] A,
  input  Bit,
  output O
);

  wire eq32_1_o;
  wire [31:0] bit_extender_1_out;

  assign bit_extender_1_out = {{31{Bit}}, Bit};  // Bit_Extender bit_extender_1
  Eq32 eq32_1 (.A(A), .B(bit_extender_1_out), .O(eq32_1_o));
  xor xor_1 (O, A[31], eq32_1_o);
endmodule

module Gt32 (
  input  [31:0] A,
  input  Bit,
  output O
);

  wire le32_1_o;

  Le32 le32_1 (.A(A), .Bit(Bit), .O(le32_1_o));
  not not_1 (O, le32_1_o);
endmodule

module Equality3 (
  input  bit2,
  input  bit1,
  input  bit0,
  output O
);

  wire and_1_out, and_2_out, not_1_out, not_2_out, not_3_out;

  not not_1 (not_1_out, bit2);
  not not_2 (not_2_out, bit1);
  not not_3 (not_3_out, bit0);
  and and_1 (and_1_out, not_1_out, not_2_out, not_3_out);
  and and_2 (and_2_out, bit2, bit1, bit0);
  or or_1 (O, and_1_out, and_2_out);
endmodule

module Shifters (
  input  [31:0] B,
  input  [4:0] Sa,
  input  [3:0] Op,
  output [31:0] O,
  output V
);

  wire multiplexer_3_out, not_1_out, or_1_out;
  wire [31:0] leftshift32_1_c, multiplexer_1_out;

  Multiplexer #(.width(32), .enable("false")) multiplexer_1 (
    .in0({B[0], B[1], B[2], B[3], B[4], B[5], B[6], B[7], B[8], B[9], B[10], B[11], B[12], B[13], B[14], B[15], B[16], B[17], B[18], B[19], B[20], B[21], B[22], B[23], B[24], B[25], B[26], B[27], B[28], B[29], B[30], B[31]}),
    .in1(B), .out(multiplexer_1_out), .sel(Op[3]));
  LeftShift32 leftshift32_1 (.Sa(Sa), .B(multiplexer_1_out), .Cin(multiplexer_3_out), .C(leftshift32_1_c));
  Multiplexer #(.width(32), .enable("false")) multiplexer_2 (
    .in0({leftshift32_1_c[0], leftshift32_1_c[1], leftshift32_1_c[2], leftshift32_1_c[3], leftshift32_1_c[4], leftshift32_1_c[5], leftshift32_1_c[6], leftshift32_1_c[7], leftshift32_1_c[8], leftshift32_1_c[9], leftshift32_1_c[10], leftshift32_1_c[11], leftshift32_1_c[12], leftshift32_1_c[13], leftshift32_1_c[14], leftshift32_1_c[15], leftshift32_1_c[16], leftshift32_1_c[17], leftshift32_1_c[18], leftshift32_1_c[19], leftshift32_1_c[20], leftshift32_1_c[21], leftshift32_1_c[22], leftshift32_1_c[23], leftshift32_1_c[24], leftshift32_1_c[25], leftshift32_1_c[26], leftshift32_1_c[27], leftshift32_1_c[28], leftshift32_1_c[29], leftshift32_1_c[30], leftshift32_1_c[31]}),
    .in1(leftshift32_1_c), .out(O), .sel(Op[3]));
  not not_1 (not_1_out, Op[0]);
  or or_1 (or_1_out, not_1_out, Op[1], Op[2]);
  Multiplexer #(.enable("false")) multiplexer_3 (.in0(B[31]), .in1(Op[1]), .out(multiplexer_3_out), .sel(or_1_out));

  assign V = Op[1];
endmodule
